# Fritzing sketch RX (saved by Fritzing 0.9.3b)
breadboards: 1

parts:
  Componente1 = Arduino Uno (Rev3)
  GLCD_128x1 = LCD screen
  R1 = Resistor [tolerance=±5% resistance=220 package=THT]
  R2 = Resistor [tolerance=±5% resistance=1M package=THT]
  J1 = Piezo Speaker
  RXRadio = IC, SIP package, 3 pins

nets:
  N1: Componente1.D9_PWM, RXRadio.pin2
  N2: Componente1.D10_PWM/SS, J1.pin2
  N3: Componente1.D11_PWM/MOSI, GLCD_128x1.E
  N4: Componente1.D12/MISO, GLCD_128x1.RS
  GND: Componente1.GND, GLCD_128x1.VSS, GLCD_128x1.R/W, GLCD_128x1.LED-, J1.pin1, RXRadio.pin1
  N5: Componente1.D2, GLCD_128x1.DB7
  N6: Componente1.D3_PWM, GLCD_128x1.DB6
  N7: Componente1.D4, GLCD_128x1.DB5
  N8: Componente1.D5_PWM, GLCD_128x1.DB4
  5V: Componente1.5V, GLCD_128x1.VDD, R1.Pin_1, R2.Pin_1, RXRadio.pin3
  N9: GLCD_128x1.V0, R2.Pin_0
  N10: GLCD_128x1.LED+, R1.Pin_0
