# Fritzing sketch TX (saved by Fritzing 0.9.3b)
breadboards: 1

parts:
  Componente1 = Arduino Nano (Rev3.0)
  TxRadio = IC, SIP package, 3 pins
  RainSensor = IC, SIP package, 4 pins
  R1 = Resistor [tolerance=±5% resistance=220 package=THT]
  LED1 = LED - 5mm [color="Red (633nm)" package="5 mm [THT]"]

nets:
  N1: Componente1.D9, TxRadio.pin2
  N2: Componente1.GND, TxRadio.pin3, RainSensor.pin2, LED1.anode
  N3: Componente1.5V, TxRadio.pin1, RainSensor.pin1, R1.Pin_1
  N4: Componente1.A0, RainSensor.pin4
  N5: R1.Pin_0, LED1.cathode
